# Fritzing sketch dotstar-74LVC125 (saved by Fritzing 0.9.3b)
breadboards: 1

parts:
  Raspberry_Pi_Zero1 = Raspberry Pi Zero
  LPD8806_RGB_LED_Strip1 = LPD8806 RGB LED Strip
  J1 = Power Jack [package=power_jack_pth]
  IC2 = IC, DIP package, 14 pins [chip_label=74AHC125]
  C2 = Electrolytic Capacitor [capacitance=1mF package="100 mil [THT, electrolytic]"]

nets:
  GND: Raspberry_Pi_Zero1.GND, LPD8806_RGB_LED_Strip1.GND, J1.PWR, IC2.pin1, IC2.pin4, IC2.pin7, C2.-
  N1: Raspberry_Pi_Zero1.GPIO10, IC2.pin2
  N2: Raspberry_Pi_Zero1.GPIO11, IC2.pin5
  N3: LPD8806_RGB_LED_Strip1.DI, IC2.pin3
  N4: LPD8806_RGB_LED_Strip1.CI, IC2.pin6
  N5: IC2.pin14, C2.+

custom parts:
  LPD8806 RGB LED Strip: Digitally addressable RGB LED strip
